# Fritzing sketch Diagrama circuital Radar arduino (saved by Fritzing 0.9.3b)

parts:
  Part1 = Arduino Uno (Rev3)
  HC-SR04_Sensor_2 = HC-SR04 Ultrasonic Distance Sensor
  HC-SR04_Sensor_1 = HC-SR04 Ultrasonic Distance Sensor
  VCC1 = Battery  # not connected
  BATERIA_x_2_=_6V = Battery
  J1 = Basic Servo

nets:
  N1: Part1.D10_PWM/SS, HC-SR04_Sensor_1.TRIG
  N2: Part1.D11_PWM/MOSI, HC-SR04_Sensor_1.ECHO
  N3: Part1.D12/MISO, J1.pulse
  N4: Part1.D5_PWM, HC-SR04_Sensor_2.TRIG
  N5: Part1.D6_PWM, HC-SR04_Sensor_2.ECHO
  5V: Part1.5V, HC-SR04_Sensor_2.VCC
  GND: Part1.GND, HC-SR04_Sensor_2.GND, BATERIA_x_2_=_6V.-
